# Fritzing sketch Breadboard_Diagrams (saved by Fritzing 0.9.3b)
breadboards: 1

parts:
  R1 = Temperature Sensor (Thermistor) [thermistor_type=NTC package=THT]
  Part1 = Arduino Uno (Rev3)
  R2 = Resistor [tolerance=±1% resistance=10k package=THT]
  Part2 = Adafruit MicroSD card breakout board [part_number="Adafruit #254"]
  R3 = Rotary Potentiometer (Small) [maximum_resistance=100kΩ package=THT]
  IC1 = ULN2003A [package="DIP16 [THT]"]
  M1 = DC Motor

nets:
  N1: R1.pin_0, Part1.A0, R2.Pin_1
  GND: R1.pin_1, Part1.GND, Part2.GND, R3.leg1, IC1.0V
  N2: Part1.A2, R3.wiper
  N3: Part1.D10_PWM/SS, Part2.CS
  N4: Part1.D11_PWM/MOSI, Part2.DI
  N5: Part1.D12/MISO, Part2.DO
  N6: Part1.D13/SCK, Part2.CLK
  N7: Part1.D4, IC1.In_1
  5V: Part1.5V, R2.Pin_0, Part2.VCC, R3.leg2, IC1.COM_-_Common, M1.pin_1
  N8: IC1.Out_1, M1.pin_2

custom parts:
  Adafruit MicroSD card breakout board: Not just a simple breakout board, this microSD adapter goes the extra mile - designed for ease of use. Onboard 5v->3v regulator provides 150mA for power-hungry cards 3v level shifting means you can use this with ease on either 3v or 5v systems Uses a proper level shifting chip, not resistors: less problems, and faster read/write access Use 3 or 4 digital pins to read and write 2Gb+ of storage!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
